# Fritzing sketch Dark_Detector_REV_A (saved by Fritzing 0.9.3b)
circuit board: 4.1369cm x 1.51599cm
breadboards: 1

parts:
  R1 = Resistor [tolerance=±5% resistance=5k package=THT]
  R2 = Resistor [tolerance=±5% resistance=100 package=THT]
  Q1 = NPN-Transistor [package="TO92 [THT]"]
  J1 = Camdenboss CTB0158-2 [part_number=CTB0158-2 package=THT]
  LDR = Photocell (LDR) [package=THT]
  J2 = Camdenboss CTB0158-2 [part_number=CTB0158-2 package=THT]

nets:
  N1: R1.Pin_0, Q1.B, LDR.pin_1
  N2: R1.Pin_1, Q1.C, J1.pin2
  N3: R2.Pin_0, J2.pin1
  N4: R2.Pin_1, Q1.E
  N5: J1.pin1, LDR.pin_0, J2.pin2

notes:
  +
  -
  PhoenixFire Computers
  REV D
  C4PT41ND34DP00L
  Dark Detector
  By:
  Dark Detector, Photo Resistive circuit, D
