# Fritzing sketch Dark_Detector_V_2_REV_A (saved by Fritzing 0.9.3b)
circuit board: 3.8292cm x 2.63085cm
breadboards: 1

parts:
  R1 = Resistor [tolerance=±5% resistance=5k package=THT]
  D1 = Rectifier Diode [part_number=1N4001 package="300 mil [THT]"]
  R2 = Resistor [tolerance=±5% resistance=220 package=THT]
  Q1 = NPN-Transistor [package="TO92 [THT]"]
  J1 = Camdenboss CTB0158-2 [part_number=CTB0158-2 package=THT]
  R3 = Photocell (LDR) [package=THT]
  J2 = Camdenboss CTB0158-2 [part_number=CTB0158-2 package=THT]

nets:
  N1: R1.Pin_0, Q1.B, R3.pin_1
  N2: R1.Pin_1, D1.cathode, Q1.C
  N3: D1.anode, J1.pin2
  N4: R2.Pin_0, J2.pin1
  N5: R2.Pin_1, Q1.E
  N6: J1.pin1, R3.pin_0, J2.pin2

notes:
  +
  -
  PhoenixFire Computers
  REV A
