# Fritzing sketch Dark_Detector_V_3_REV_A (saved by Fritzing 0.9.3b)
circuit board: 5.41231cm x 1.07439cm
breadboards: 1

parts:
  J1 = Camdenboss CTB0158-2 [part_number=CTB0158-2 package=THT]
  D1 = Rectifier Diode [part_number=1N4001 package="300 mil [THT]"]
  R1 = Resistor [tolerance=±5% resistance=220 package=THT]
  R2 = Resistor [tolerance=±5% resistance=220 package=THT]
  Q1 = NPN-Transistor [package="TO92 [THT]"]
  R3 = Photocell (LDR) [package=THT]
  J2 = Camdenboss CTB0158-2 [part_number=CTB0158-2 package=THT]

nets:
  N1: J1.pin1, R3.pin_0, J2.pin2
  N2: J1.pin2, D1.anode
  N3: D1.cathode, R1.Pin_1, Q1.C
  N4: R1.Pin_0, Q1.B, R3.pin_1
  N5: R2.Pin_0, J2.pin1
  N6: R2.Pin_1, Q1.E
